# Fritzing sketch Conexiones (saved by Fritzing 0.9.6b)
breadboards: 1

parts:
  Componente1 = Arduino Uno (Rev3) - ICSP
  U1 = LCD-16X2 [package=lcd-16x2_noholes]
  HC-SR04_Sensor_1 = HC-SR04 Ultrasonic Distance Sensor
  LED1 = LED - 5mm [color="Red (633nm)" current=0.030 package="5 mm [THT]"]
  Componente2 = Thumb Joystick
  RHT1 = Humidity and Temperature Sensor RHT03
  S1 = Pushbutton [package="[SMD]"]
  LED2 = LEDs [package=led10mm]
  R1 = Rotary Potentiometer (Small) [maximum_resistance=100kΩ package=THT]
  R2 = Resistor [tolerance=±5% resistance=220 package="2010 [SMD]"]
  R3 = Resistor [tolerance=±5% resistance=220 package="2010 [SMD]"]
  R4 = Resistor [tolerance=±5% resistance=220 package="2010 [SMD]"]
  R5 = Resistor [tolerance=±5% resistance=220 package="2010 [SMD]"]
  R6 = Resistor [tolerance=±5% resistance=220 package="2010 [SMD]"]

nets:
  N1: Componente1.A0, Componente2.HORZ
  N2: Componente1.A1, Componente2.VERT
  N3: Componente1.D8, Componente2.SEL
  N4: Componente1.D9_PWM, HC-SR04_Sensor_1.TRIG
  N5: Componente1.D10_PWM/SS, HC-SR04_Sensor_1.ECHO
  N6: Componente1.D11_PWM/MOSI, S1.Pin_3, S1.Pin_4, R3.Pin_1
  N7: Componente1.D12/MISO, RHT1.Data-signal, R6.Pin_0
  GND: Componente1.GND, U1.VSS, U1.R_W, U1.K, HC-SR04_Sensor_1.GND, LED1.cathode, Componente2.GND, RHT1.GND_2, S1.Pin_1, S1.Pin_2, LED2.C, R1.leg1
  N8: Componente1.D0/RX, R4.Pin_1
  N9: Componente1.D1/TX, R5.Pin_1
  N10: Componente1.D2, U1.DB7
  N11: Componente1.D3_PWM, U1.DB6
  N12: Componente1.D4, U1.DB5
  N13: Componente1.D5_PWM, U1.DB4
  N14: Componente1.D6_PWM, U1.E
  N15: Componente1.D7, U1.RS
  VCC: Componente1.5V, U1.VDD, HC-SR04_Sensor_1.VCC, Componente2.VCC, RHT1.Vcc, R1.leg2, R2.Pin_0, R3.Pin_0, R6.Pin_1
  N16: U1.VO, R1.wiper
  N17: U1.A, R2.Pin_1
  N18: LED1.anode, R4.Pin_0
  N19: LED2.A, R5.Pin_0
